// Logisim project hw2.circ as structural Verilog: 12 circuits, main circuit main
module main (
  input  O3,
  input  O2,
  input  O1,
  input  O0,
  input  A1,
  input  A0,
  input  B1,
  input  B0,
  output P,
  output Z,
  output L0,
  output L1,
  output L2,
  output L3,
  output L4,
  output L5,
  output L6,
  output L7,
  output L8,
  output L9,
  output E,
  output G,
  output L,
  output S,
  output C
);

  wire adder_1_addo0, adder_1_addo1, and_1_ando0, and_1_ando1, divisior_1_div0, divisior_1_div1,
       modulo_1_mod0, modulo_1_mod1, multip_1_multo0, multip_1_multo1, multip_1_multo2, multip_1_multo3,
       n1to9_1__1to9o0, n1to9_1__1to9o1, n1to9_1__1to9o2, n1to9_1__1to9o3, n1to9_1__1to9o4, n1to9_1__1to9o5,
       n1to9_1__1to9o6, n1to9_1__1to9o7, n1to9_1__1to9o8, n8or_1__8oroutput, n8or_2__8oroutput, or_1_oro0,
       or_1_oro1, or_2_out, subtractor_1_subo0, subtractor_1_subo1, xor_1_xoro0, xor_1_xoro1;

  _1to9 u_1to9_1 (
    ._1to9i0(O0), ._1to9i1(O1), ._1to9i2(O2), ._1to9i3(O3), ._1to9Cancel(1'b0), ._1to9o0(n1to9_1__1to9o0),
    ._1to9o1(n1to9_1__1to9o1), ._1to9o2(n1to9_1__1to9o2), ._1to9o3(n1to9_1__1to9o3),
    ._1to9o4(n1to9_1__1to9o4), ._1to9o5(n1to9_1__1to9o5), ._1to9o6(n1to9_1__1to9o6),
    ._1to9o7(n1to9_1__1to9o7), ._1to9o8(n1to9_1__1to9o8));  // open: _1to9o9
  modulo modulo_1 (
    .modA1(A1), .modA0(A0), .modB1(B1), .modB0(B0), .modEnable(n1to9_1__1to9o0), .mod1(modulo_1_mod1),
    .mod0(modulo_1_mod0));
  multip multip_1 (
    .multA1(A1), .multA0(A0), .multB1(B1), .multB0(B0), .multEnable(n1to9_1__1to9o1),
    .multO3(multip_1_multo3), .multO2(multip_1_multo2), .multO1(multip_1_multo1), .multO0(multip_1_multo0));
  divisior divisior_1 (
    .divA1(A1), .divA0(A0), .divB1(B1), .divB0(B0), .divEnable(n1to9_1__1to9o2), .div1(divisior_1_div1),
    .div0(divisior_1_div0));
  adder adder_1 (
    .addA1(A1), .addA0(A0), .addB1(B1), .addB0(B0), .addEnable(n1to9_1__1to9o3), .addCarry(C),
    .addO1(adder_1_addo1), .addO0(adder_1_addo0));
  subtractor subtractor_1 (
    .subA1(A1), .subA0(A0), .subB1(B1), .subB0(B0), .subEnable(n1to9_1__1to9o4), .subSign(S),
    .subO1(subtractor_1_subo1), .subO0(subtractor_1_subo0));
  comparison comparison_1 (
    .compA1(A1), .compA0(A0), .compB1(B1), .compB0(B0), .compEnable(n1to9_1__1to9o5), .compGreater(G),
    .compEq(E), .compLess(L));
  \and  and_1 (
    .andA1(A1), .andA0(A0), .andB1(B1), .andB0(B0), .andEnable(n1to9_1__1to9o6), .andO1(and_1_ando1),
    .andO0(and_1_ando0));
  \xor  xor_1 (
    .xorA1(A1), .xorA0(A0), .xorB1(B1), .xorB0(B0), .xorEnable(n1to9_1__1to9o7), .xorO1(xor_1_xoro1),
    .xorO0(xor_1_xoro0));
  \or  or_1 (
    .orA1(A1), .orA0(A0), .orB1(B1), .orB0(B0), .orEnable(n1to9_1__1to9o8), .orO1(or_1_oro1), .orO0(or_1_oro0));
  _8or u_8or_1 (
    ._8or0(modulo_1_mod0), ._8or1(multip_1_multo0), ._8or2(divisior_1_div0), ._8or3(adder_1_addo0),
    ._8or4(subtractor_1_subo0), ._8or5(and_1_ando0), ._8or6(xor_1_xoro0), ._8or7(or_1_oro0),
    ._8orOutput(n8or_1__8oroutput));
  _8or u_8or_2 (
    ._8or0(modulo_1_mod1), ._8or1(multip_1_multo1), ._8or2(divisior_1_div1), ._8or3(adder_1_addo1),
    ._8or4(subtractor_1_subo1), ._8or5(and_1_ando1), ._8or6(xor_1_xoro1), ._8or7(or_1_oro1),
    ._8orOutput(n8or_2__8oroutput));
  or or_2 (or_2_out, multip_1_multo2, C);
  _1to9 u_1to9_2 (
    ._1to9i0(n8or_1__8oroutput), ._1to9i1(n8or_2__8oroutput), ._1to9i2(or_2_out), ._1to9i3(multip_1_multo3),
    ._1to9Cancel(n1to9_1__1to9o5), ._1to9o0(L0), ._1to9o1(L1), ._1to9o2(L2), ._1to9o3(L3), ._1to9o4(L4),
    ._1to9o5(L5), ._1to9o6(L6), ._1to9o7(L7), ._1to9o8(L8), ._1to9o9(L9));
  _8or u_8or_3 (
    ._8or0(1'b0), ._8or1(1'b0), ._8or2(1'b0), ._8or3(L8), ._8or4(L7), ._8or5(L4), ._8or6(L2), ._8or7(L1),
    ._8orOutput(P));

  assign Z = L0;
endmodule

module modulo (
  input  modEnable,
  input  modA1,
  input  modA0,
  input  modB1,
  input  modB0,
  output mod1,
  output mod0
);

  wire and_1_out, n4_to_1_mux_x2_74153_1_p9, not_1_out;

  not not_1 (not_1_out, modB0);
  and and_1 (and_1_out, modB1, modB0);
  // _4_to_1_MUX__x2___74153 #(.Facing("east")) 4_to_1_mux_x2_74153_1: pin names not known; wires that end beside it: 1'b0, 1'b0, and_1_out, 1'b0, 1'b0, modB1, 1'b0, not_1_out, n4_to_1_mux_x2_74153_1_p9, modA0, n4_to_1_mux_x2_74153_1_p9, modA1, mod1, mod0
  not not_2 (n4_to_1_mux_x2_74153_1_p9, modEnable);
endmodule

module multip (
  input  multA1,
  input  multA0,
  input  multB1,
  input  multB0,
  input  multEnable,
  output multO3,
  output multO2,
  output multO1,
  output multO0
);

  wire and_1_out, and_2_out, not_1_out, not_2_out, xor_1_out;

  not not_1 (not_1_out, multB0);
  and and_1 (and_1_out, multB0, multB1);
  and and_2 (and_2_out, not_1_out, multB1);
  xor xor_1 (xor_1_out, multB0, multB1);
  not not_2 (not_2_out, multEnable);
  // _4_to_1_MUX__x2___74153 #(.Facing("east")) 4_to_1_mux_x2_74153_1: pin names not known; wires that end beside it: 1'b0, 1'b0, 1'b0, and_1_out, 1'b0, 1'b0, multB1, and_2_out, not_2_out, multA0, not_2_out, multA1, multO3, multO2
  // _4_to_1_MUX__x2___74153 #(.Facing("east")) 4_to_1_mux_x2_74153_2: pin names not known; wires that end beside it: 1'b0, multB1, multB0, xor_1_out, 1'b0, multB0, 1'b0, multB0, not_2_out, multA0, not_2_out, multA1, multO1, multO0
endmodule

module divisior (
  input  divEnable,
  input  divA1,
  input  divA0,
  input  divB1,
  input  divB0,
  output div1,
  output div0
);

  wire not_1_out, not_2_out, not_3_out;

  not not_1 (not_1_out, divB1);
  not not_2 (not_2_out, divB0);
  not not_3 (not_3_out, divEnable);
  // _4_to_1_MUX__x2___74153 #(.Facing("east")) 4_to_1_mux_x2_74153_1: pin names not known; wires that end beside it: 1'b0, 1'b0, not_1_out, not_1_out, 1'b0, not_1_out, not_2_out, 1'b1, not_3_out, divA0, not_3_out, divA1, div1, div0
endmodule

module adder (
  input  addA1,
  input  addA0,
  input  addB1,
  input  addB0,
  input  addEnable,
  output addCarry,
  output addO1,
  output addO0
);

  wire and_1_out, not_1_out, not_2_out, not_3_out, not_4_out, or_1_out, xor_1_out;

  xor xor_1 (xor_1_out, addB0, addB1);
  and and_1 (and_1_out, addB0, addB1);
  or or_1 (or_1_out, addB0, addB1);
  not not_1 (not_1_out, addB1);
  not not_2 (not_2_out, xor_1_out);
  not not_3 (not_3_out, addB0);
  not not_4 (not_4_out, addEnable);
  // _4_to_1_MUX__x2___74153 #(.Facing("east")) 4_to_1_mux_x2_74153_1: pin names not known; wires that end beside it: 1'b0, and_1_out, addB1, or_1_out, addB1, xor_1_out, not_1_out, not_2_out, not_4_out, addA0, not_4_out, addA1, addCarry, addO1
  // _4_to_1_MUX__x2___74153 #(.Facing("east")) 4_to_1_mux_x2_74153_2: pin names not known; wires that end beside it: addB0, not_3_out, addB0, not_3_out, 1'b0, 1'b0, 1'b0, 1'b0, not_4_out, addA0, 1'b1, addA1, addO0
endmodule

module subtractor (
  input  subA1,
  input  subA0,
  input  subB1,
  input  subB0,
  input  subEnable,
  output subSign,
  output subO1,
  output subO0
);

  wire and_1_out, and_2_out, n4_to_1_mux_x2_74153_1_p8, not_1_out, not_2_out, not_3_out, not_4_out, or_1_out;

  and and_1 (and_1_out, subB0, subB1);
  not not_1 (not_1_out, subB0);
  or or_1 (or_1_out, subB0, subB1);
  and and_2 (and_2_out, not_1_out, not_2_out);
  not not_2 (not_2_out, subB1);
  not not_3 (not_3_out, subB0);
  not not_4 (not_4_out, subEnable);
  // _4_to_1_MUX__x2___74153 #(.Facing("east")) 4_to_1_mux_x2_74153_1: pin names not known; wires that end beside it: or_1_out, subB1, and_1_out, 1'b0, subB1, and_1_out, and_2_out, n4_to_1_mux_x2_74153_1_p8, not_4_out, subA0, not_4_out, subA1, subSign, subO1
  not not_5 (n4_to_1_mux_x2_74153_1_p8, subB1);
  // _4_to_1_MUX__x2___74153 #(.Facing("east")) 4_to_1_mux_x2_74153_2: pin names not known; wires that end beside it: subB0, not_3_out, subB0, not_3_out, 1'b0, 1'b0, 1'b0, 1'b0, not_4_out, subA0, 1'b1, subA1, subO0
endmodule

module comparison (
  input  compA1,
  input  compA0,
  input  compEnable,
  input  compB1,
  input  compB0,
  output compGreater,
  output compEq,
  output compLess
);

  wire and_1_out, and_3_out, not_1_out, not_2_out, not_3_out, not_4_out, or_1_out, xnor_1_out, xnor_2_out;

  and and_1 (and_1_out, compB0, compB1);
  or or_1 (or_1_out, compB0, compB1);
  not not_1 (not_1_out, and_1_out);
  not not_2 (not_2_out, or_1_out);
  not not_3 (not_3_out, compB1);
  not not_4 (not_4_out, compEnable);
  // _4_to_1_MUX__x2___74153 #(.Facing("east")) 4_to_1_mux_x2_74153_1: pin names not known; wires that end beside it: compB0, 1'b0, not_2_out, not_3_out, not_1_out, or_1_out, compB1, and_1_out, 1'b0, not_4_out, compA0, not_4_out, compA1, compGreater, compLess
  and and_2 (compEq, and_3_out, compEnable);
  and and_3 (and_3_out, xnor_1_out, xnor_2_out);
  xnor xnor_1 (xnor_1_out, compA0, compB0);
  xnor xnor_2 (xnor_2_out, compA1, compB1);
endmodule

module \and  (
  input  andEnable,
  input  andA1,
  input  andA0,
  input  andB1,
  input  andB0,
  output andO1,
  output andO0
);

  wire and_1_out, and_2_out;

  and and_1 (and_1_out, andA1, andB1);
  and and_2 (and_2_out, andA0, andB0);
  and and_3 (andO1, andEnable, and_1_out);
  and and_4 (andO0, andEnable, and_2_out);
endmodule

module \or  (
  input  orEnable,
  input  orA1,
  input  orA0,
  input  orB1,
  input  orB0,
  output orO1,
  output orO0
);

  wire or_1_out, or_2_out;

  or or_1 (or_1_out, orA1, orB1);
  or or_2 (or_2_out, orA0, orB0);
  and and_1 (orO1, orEnable, or_1_out);
  and and_2 (orO0, orEnable, or_2_out);
endmodule

module \xor  (
  input  xorEnable,
  input  xorA1,
  input  xorA0,
  input  xorB1,
  input  xorB0,
  output xorO1,
  output xorO0
);

  wire xor_1_out, xor_2_out;

  xor xor_1 (xor_1_out, xorA1, xorB1);
  xor xor_2 (xor_2_out, xorA0, xorB0);
  and and_1 (xorO1, xorEnable, xor_1_out);
  and and_2 (xorO0, xorEnable, xor_2_out);
endmodule

module _1to9 (
  input  _1to9i0,
  input  _1to9i1,
  input  _1to9i2,
  input  _1to9i3,
  input  _1to9Cancel,
  output _1to9o0,
  output _1to9o1,
  output _1to9o2,
  output _1to9o3,
  output _1to9o4,
  output _1to9o5,
  output _1to9o6,
  output _1to9o7,
  output _1to9o8,
  output _1to9o9
);

  wire and_1_out, and_2_out, n3_to_8_decoder_74138_1_p4, n3_to_8_decoder_74138_1_p7,
       n3_to_8_decoder_74138_1_p8, n3_to_8_decoder_74138_1_p9, n3_to_8_decoder_74138_1_p10,
       n3_to_8_decoder_74138_1_p11, n3_to_8_decoder_74138_1_p12, n3_to_8_decoder_74138_1_p13,
       n3_to_8_decoder_74138_1_p14, not_2_out, not_3_out;

  // _3_to_8_decoder__74138 #(.Facing("east")) 3_to_8_decoder_74138_1: pin names not known; wires that end beside it: _1to9i0, _1to9i1, _1to9i2, n3_to_8_decoder_74138_1_p4, _1to9Cancel, _1to9Cancel, n3_to_8_decoder_74138_1_p7, n3_to_8_decoder_74138_1_p8, n3_to_8_decoder_74138_1_p9, n3_to_8_decoder_74138_1_p10, n3_to_8_decoder_74138_1_p11, n3_to_8_decoder_74138_1_p12, n3_to_8_decoder_74138_1_p13, n3_to_8_decoder_74138_1_p14
  not not_1 (n3_to_8_decoder_74138_1_p4, _1to9i3);
  not not_2 (not_2_out, _1to9Cancel);
  and and_1 (and_1_out, _1to9i3, not_3_out);
  not not_3 (not_3_out, _1to9i0);
  and and_2 (and_2_out, _1to9i3, _1to9i0);
  and and_3 (_1to9o8, not_2_out, and_1_out);
  and and_4 (_1to9o9, not_2_out, and_2_out);
  not not_4 (_1to9o0, n3_to_8_decoder_74138_1_p7);
  not not_5 (_1to9o1, n3_to_8_decoder_74138_1_p8);
  not not_6 (_1to9o2, n3_to_8_decoder_74138_1_p9);
  not not_7 (_1to9o3, n3_to_8_decoder_74138_1_p10);
  not not_8 (_1to9o4, n3_to_8_decoder_74138_1_p11);
  not not_9 (_1to9o5, n3_to_8_decoder_74138_1_p12);
  not not_10 (_1to9o6, n3_to_8_decoder_74138_1_p13);
  not not_11 (_1to9o7, n3_to_8_decoder_74138_1_p14);
endmodule

module _8or (
  input  _8or0,
  input  _8or1,
  input  _8or2,
  input  _8or3,
  input  _8or4,
  input  _8or5,
  input  _8or6,
  input  _8or7,
  output _8orOutput
);

  wire or_1_out, or_2_out, or_3_out, or_4_out, or_5_out, or_6_out;

  or or_1 (or_1_out, _8or0, _8or1);
  or or_2 (or_2_out, _8or2, _8or3);
  or or_3 (or_3_out, _8or4, _8or5);
  or or_4 (or_4_out, _8or6, _8or7);
  or or_5 (or_5_out, or_1_out, or_2_out);
  or or_6 (or_6_out, or_3_out, or_4_out);
  or or_7 (_8orOutput, or_5_out, or_6_out);
endmodule
